// Logisim project s-mips.circ as structural Verilog
module S_MIPS_Board (
  output halt
);

  wire button_1_out, CLK, CS, d_ff_1_q, R_W, Reset_out, RST, TTY_EN;
  wire [2:0] KDB;
  wire [3:0] Mask, ram_1_read_time, ram_1_write_time;
  wire [6:0] KDB_DATA, TTY_DATA;
  wire [15:0] Addr;
  wire [31:0] ram_1_data_out_0, ram_1_data_out_1, ram_1_data_out_2, ram_1_data_out_3, s_mips_1_ram_in_0,
       s_mips_1_ram_in_1, s_mips_1_ram_in_2, s_mips_1_ram_in_3;

  TTY #(.rows(25), .cols(80)) tty_1 (.data(TTY_DATA), .clk(CLK), .we(TTY_EN), .clr(RST));
  RAM ram_1 (
    .Address(Addr), .Data_Out_0(ram_1_data_out_0), .Data_Out_1(ram_1_data_out_1),
    .Data_Out_2(ram_1_data_out_2), .Data_Out_3(ram_1_data_out_3), .Data_In_0(s_mips_1_ram_in_0),
    .Data_In_1(s_mips_1_ram_in_1), .Data_In_2(s_mips_1_ram_in_2), .Data_In_3(s_mips_1_ram_in_3), .Mask(Mask),
    .nRead_Write(R_W), .Chip_Select(CS), .Read_Time(ram_1_read_time), .Reset(button_1_out),
    .Write_Time(ram_1_write_time));
  Button button_1 (.out(button_1_out));
  Keyboard #(.buflen(64)) keyboard_1 (.clk(CLK), .re(KDB[0]), .avail(KDB[2]), .data(KDB_DATA));  // open: clr
  S_MIPS s_mips_1 (
    .Kbd_Enable(KDB[0]), .Address(Addr), .Kbd_Clear(KDB[1]), .Kbd_Available(KDB[2]),
    .RAM_In_0(s_mips_1_ram_in_0), .Kbd_ASCII_Data(KDB_DATA), .RAM_In_1(s_mips_1_ram_in_1),
    .TTY_Enable(TTY_EN), .RAM_In_2(s_mips_1_ram_in_2), .RAM_In_3(s_mips_1_ram_in_3),
    .TTY_ASCII_Data(TTY_DATA), .Reset(RST), .RAM_Out_0(ram_1_data_out_0), .Clock(CLK),
    .RAM_Out_1(ram_1_data_out_1), .Stop(halt), .RAM_Out_2(ram_1_data_out_2), .RAM_Out_3(ram_1_data_out_3),
    .Mask(Mask), .Read_Time(ram_1_read_time), .Write_Time(ram_1_write_time), .nRead_Write(R_W),
    .Chip_Select(CS));
  D_Flip_Flop d_ff_1 (.clk(CLK), .D(1'b1), .Q(d_ff_1_q), .reset(Reset_out));  // open: Qn, preset, en
  Button Reset (.out(Reset_out));
  Clock clock_1 (.out(CLK));
  D_Flip_Flop d_ff_2 (.clk(CLK), .D(d_ff_1_q), .Qn(RST), .reset(Reset_out));  // open: Q, preset, en

  // Notes on the sheet:
  //   NO MODIFICAR
  //   Keyboard
endmodule

module RAM (
  input  [15:0] Address,
  input  [31:0] Data_In_0,
  input  [31:0] Data_In_1,
  input  [31:0] Data_In_2,
  input  [31:0] Data_In_3,
  input  [3:0] Mask,
  input  nRead_Write,
  input  Chip_Select,
  input  Reset,
  output [31:0] Data_Out_0,
  output [31:0] Data_Out_1,
  output [31:0] Data_Out_2,
  output [31:0] Data_Out_3,
  output [3:0] Read_Time,
  output [3:0] Write_Time
);

  wire and_2_out, and_3_out, and_4_out, and_5_out, and_6_out, and_7_out, and_8_out, and_9_out, Changed, CLK,
       comparator_2_eq, comparator_3_eq, comparator_4_eq, comparator_5_eq, comparator_6_eq, Count,
       demultiplexer_3_out0, Idle, Idle_q, Load, Load0, Load1, nand_1_out, or_1_out, or_2_out, or_3_out,
       or_4_out, or_5_out, or_6_out, or_7_out, or_8_out, or_9_out, or_10_out, Proc_q, Update_Mem, Zero_Time;
  wire [3:0] counter_1_q, multiplexer_1_out, subtractor_1_out;
  wire [31:0] register_1_q, register_2_q, register_3_q, register_4_q, register_5_q;

  // Probe on 4'b0011
  // Probe on 4'b0101
  Multiplexer #(.width(4), .enable("false")) multiplexer_1 (
    .in0(4'b0011), .in1(4'b0101), .out(multiplexer_1_out), .sel(nRead_Write));
  or or_1 (or_1_out, Idle, Update_Mem);
  or or_2 (or_2_out, ~Chip_Select, Reset);  // OR_Gate
  Subtractor #(.width(4)) subtractor_1 (.a(multiplexer_1_out), .b(4'b0010), .out(subtractor_1_out));  // open: bin, bout
  Demultiplexer #(.enable("false")) demultiplexer_1 (.out0(Idle), .out1(Load0), .in(Idle_q), .sel(Changed));
  D_Flip_Flop u_Idle (.clk(CLK), .D(or_1_out), .Q(Idle_q), .preset(or_2_out));  // open: Qn, en, reset
  // Probe on counter_1_q
  Counter #(.width(4), .max('hf)) counter_1 (
    .load(Load), .D(subtractor_1_out), .count(Count), .Q(counter_1_q), .clk(CLK), .clr(or_3_out));  // open: carry
  or or_3 (or_3_out, ~Chip_Select, Reset);  // OR_Gate
  Comparator #(.width(4), .mode("unsigned")) comparator_1 (
    .a(4'b0000), .b(counter_1_q), .eq(Zero_Time));  // open: gt, lt
  or or_4 (or_4_out, Count, Load0, Load1);
  Register #(.width(32)) register_1 (.D(Data_In_0), .en(Chip_Select), .Q(register_1_q), .clk(CLK), .clr(or_5_out));
  or or_5 (or_5_out, ~Chip_Select, Reset);  // OR_Gate
  Register #(.width(32)) register_2 (.D(Data_In_1), .en(Chip_Select), .Q(register_2_q), .clk(CLK), .clr(or_6_out));
  or or_6 (or_6_out, ~Chip_Select, Reset);  // OR_Gate
  Register #(.width(32)) register_3 (.D(Data_In_2), .en(Chip_Select), .Q(register_3_q), .clk(CLK), .clr(or_7_out));
  or or_7 (or_7_out, ~Chip_Select, Reset);  // OR_Gate
  Register #(.width(32)) register_4 (.D(Data_In_3), .en(Chip_Select), .Q(register_4_q), .clk(CLK), .clr(or_8_out));
  or or_8 (or_8_out, ~Chip_Select, Reset);  // OR_Gate
  Register #(.width(32)) register_5 (
    .D({{11{1'b1}}, nRead_Write, Mask, Address}), .en(Chip_Select), .Q(register_5_q), .clk(CLK),
    .clr(or_9_out));
  or or_9 (or_9_out, ~Chip_Select, Reset);  // OR_Gate
  D_Flip_Flop Proc (.clk(CLK), .D(or_4_out), .Q(Proc_q), .reset(or_10_out));  // open: Qn, preset, en
  or or_10 (or_10_out, ~Chip_Select, Reset);  // OR_Gate
  Demultiplexer #(.enable("false")) demultiplexer_2 (
    .out0(Count), .out1(Update_Mem), .in(demultiplexer_3_out0), .sel(Zero_Time));
  Demultiplexer #(.enable("false")) demultiplexer_3 (
    .out0(demultiplexer_3_out0), .out1(Load1), .in(Proc_q), .sel(Changed));
  Clock clock_1 (.out(CLK));
  Comparator #(.width(32)) comparator_2 (.a(register_1_q), .b(Data_In_0), .eq(comparator_2_eq));  // open: gt, lt
  Comparator #(.width(32)) comparator_3 (.a(register_2_q), .b(Data_In_1), .eq(comparator_3_eq));  // open: gt, lt
  Comparator #(.width(32)) comparator_4 (.a(register_3_q), .b(Data_In_2), .eq(comparator_4_eq));  // open: gt, lt
  Comparator #(.width(32)) comparator_5 (.a(register_4_q), .b(Data_In_3), .eq(comparator_5_eq));  // open: gt, lt
  Comparator #(.width(32)) comparator_6 (
    .a(register_5_q), .b({{11{1'b1}}, nRead_Write, Mask, Address}), .eq(comparator_6_eq));  // open: gt, lt
  nand nand_1 (nand_1_out, comparator_6_eq, comparator_2_eq, comparator_3_eq, comparator_4_eq, comparator_5_eq);
  and and_1 (Changed, nand_1_out, Chip_Select);
  or or_11 (Load, Count, Load1, Load0);
  and and_2 (and_2_out, Mask[0], Update_Mem, nRead_Write);
  and and_3 (and_3_out, Mask[1], Update_Mem, nRead_Write);
  and and_4 (and_4_out, Mask[2], Update_Mem, nRead_Write);
  and and_5 (and_5_out, Mask[3], Update_Mem, nRead_Write);
  RAM_part #(.addrWidth(16), .dataWidth(32), .bus("separate")) ram_1 (
    .addr(Address), .din(Data_In_0), .data(Data_Out_0), .str(and_2_out), .sel(Chip_Select), .clk(CLK),
    .ld(and_6_out), .clr(Reset));
  and and_6 (and_6_out, ~nRead_Write, Idle);  // AND_Gate
  RAM_part #(.addrWidth(16), .dataWidth(32), .bus("separate")) ram_2 (
    .addr(Address), .din(Data_In_1), .data(Data_Out_1), .str(and_3_out), .sel(Chip_Select), .clk(CLK),
    .ld(and_7_out), .clr(Reset));
  and and_7 (and_7_out, ~nRead_Write, Idle);  // AND_Gate
  RAM_part #(.addrWidth(16), .dataWidth(32), .bus("separate")) ram_3 (
    .addr(Address), .din(Data_In_2), .data(Data_Out_2), .str(and_4_out), .sel(Chip_Select), .clk(CLK),
    .ld(and_8_out), .clr(Reset));
  and and_8 (and_8_out, ~nRead_Write, Idle);  // AND_Gate
  RAM_part #(.addrWidth(16), .dataWidth(32), .bus("separate")) ram_4 (
    .addr(Address), .din(Data_In_3), .data(Data_Out_3), .str(and_5_out), .sel(Chip_Select), .clk(CLK),
    .ld(and_9_out), .clr(Reset));
  and and_9 (and_9_out, ~nRead_Write, Idle);  // AND_Gate

  assign Read_Time = 4'b0011;
  assign Write_Time = 4'b0101;

  // Other names for the same wires on the sheet: M0 = Mask[0]; M1 = Mask[1]; M2 = Mask[2]; M3 = Mask[3];
  //   RW = nRead_Write; CLR = Reset; CS = Chip_Select; Load2 = Count

  // Notes on the sheet:
  //   NO MODIFICAR
  //   excepto quizás los valores RT y WT
  //   BANK0
  //   BANK1
  //   BANK2
  //   BANK3
endmodule

module S_MIPS (
  input  Kbd_Available,
  input  [6:0] Kbd_ASCII_Data,
  input  [31:0] RAM_Out_0,
  input  [31:0] RAM_Out_1,
  input  Reset,
  input  [31:0] RAM_Out_2,
  input  Clock,
  input  [31:0] RAM_Out_3,
  input  [3:0] Read_Time,
  input  [3:0] Write_Time,
  output Kbd_Enable,
  output [15:0] Address,
  output Kbd_Clear,
  output TTY_Enable,
  output [6:0] TTY_ASCII_Data,
  output Stop,
  output [31:0] RAM_In_0,
  output [31:0] RAM_In_1,
  output [31:0] RAM_In_2,
  output [31:0] RAM_In_3,
  output [3:0] Mask,
  output nRead_Write,
  output Chip_Select
);


  assign Address = {16{1'b0}};
  assign Chip_Select = 1'b0;
  assign Kbd_Clear = 1'b0;
  assign Kbd_Enable = 1'b1;
  assign Mask = 4'b0000;
  assign nRead_Write = 1'b0;
  assign RAM_In_0 = {32{1'b0}};
  assign RAM_In_1 = {32{1'b0}};
  assign RAM_In_2 = {32{1'b0}};
  assign RAM_In_3 = {32{1'b0}};
  assign Stop = 1'b0;
  assign TTY_Enable = 1'b0;

  // Other names for the same wires on the sheet: CLK = Clock; CLR = Reset; KBD_AVAIL = Kbd_Available;
  //   KBD_DATA[6:0] = Kbd_ASCII_Data; RAM_OUTPUT_0[31:0] = RAM_Out_0; RAM_OUTPUT_1[31:0] = RAM_Out_1;
  //   RAM_OUTPUT_2[31:0] = RAM_Out_2; RAM_OUTPUT_3[31:0] = RAM_Out_3; TTY_DATA[6:0] = TTY_ASCII_Data

  // Notes on the sheet:
  //   RAM ADDRESS
  //   DATA FROM RAM
  //   DATA TO RAM
  //   DATA WRITE MASK
  //   RAM TIMING
  //   RAM CONTROL
  //   KEYBOARD
  //   TTY
  //   SEQUENCING
  //   Esto lo tienen que borrar:
endmodule

module RegisterFile (
  input  [4:0] \Dirección_de_destino ,
  input  Read_Write,
  input  [31:0] Datos_de_entrada,
  input  [4:0] Selector_de_salida_A,
  input  [4:0] Selector_de_salida_B,
  input  Reset,
  input  Clock,
  output [31:0] Read_Data_1,
  output [31:0] Read_Data_2
);

  wire Register_0_on_off, Register_1_on_off, Register_2_on_off, Register_3_on_off, Register_4_on_off,
       Register_5_on_off, Register_6_on_off, Register_7_on_off, Register_8_on_off, Register_9_on_off,
       Register_10_on_off, Register_11_on_off, Register_12_on_off, Register_13_on_off, Register_14_on_off,
       Register_15_on_off, Register_16_on_off, Register_17_on_off, Register_18_on_off, Register_19_on_off,
       Register_20_on_off, Register_21_on_off, Register_22_on_off, Register_23_on_off, Register_24_on_off,
       Register_25_on_off, Register_26_on_off, Register_27_on_off, Register_28_on_off, Register_29_on_off,
       Register_30_on_off, Register_31_on_off;
  wire [31:0] reg0_out, reg1_out, reg2_out, reg3_out, reg3out, reg4_out, reg5_out, reg6_out, reg7_out,
       reg8_out, reg9_out, reg10_out, reg11_out, reg12_out, reg13_out, reg14_out, reg15_out, reg16_out,
       reg17_out, reg18_out, reg19_out, reg20_out, reg21_out, reg22_out, reg23_out, reg24_out, reg25_out,
       reg26_out, reg27_out, reg28_out, reg29_out, reg30_out, reg30_ut, reg31_out;

  Register #(.width(32)) register_1 (.D({32{1'b0}}), .en(Register_0_on_off), .Q(reg0_out), .clk(Clock), .clr(Reset));
  Register #(.width(32)) register_2 (
    .D(Datos_de_entrada), .en(Register_1_on_off), .Q(reg1_out), .clk(Clock), .clr(Reset));
  Register #(.width(32)) register_3 (
    .D(Datos_de_entrada), .en(Register_2_on_off), .Q(reg2_out), .clk(Clock), .clr(Reset));
  Register #(.width(32)) register_4 (
    .D(Datos_de_entrada), .en(Register_3_on_off), .Q(reg3out), .clk(Clock), .clr(Reset));
  Register #(.width(32)) register_5 (
    .D(Datos_de_entrada), .en(Register_4_on_off), .Q(reg4_out), .clk(Clock), .clr(Reset));
  Register #(.width(32)) register_6 (
    .D(Datos_de_entrada), .en(Register_5_on_off), .Q(reg5_out), .clk(Clock), .clr(Reset));
  Register #(.width(32)) register_7 (
    .D(Datos_de_entrada), .en(Register_6_on_off), .Q(reg6_out), .clk(Clock), .clr(Reset));
  Register #(.width(32)) register_8 (
    .D(Datos_de_entrada), .en(Register_7_on_off), .Q(reg7_out), .clk(Clock), .clr(Reset));
  Register #(.width(32)) register_9 (
    .D(Datos_de_entrada), .en(Register_8_on_off), .Q(reg8_out), .clk(Clock), .clr(Reset));
  Register #(.width(32)) register_10 (
    .D(Datos_de_entrada), .en(Register_9_on_off), .Q(reg9_out), .clk(Clock), .clr(Reset));
  Register #(.width(32)) register_11 (
    .D(Datos_de_entrada), .en(Register_10_on_off), .Q(reg10_out), .clk(Clock), .clr(Reset));
  Register #(.width(32)) register_12 (
    .D(Datos_de_entrada), .en(Register_11_on_off), .Q(reg11_out), .clk(Clock), .clr(Reset));
  Register #(.width(32)) register_13 (
    .D(Datos_de_entrada), .en(Register_12_on_off), .Q(reg12_out), .clk(Clock), .clr(Reset));
  Register #(.width(32)) register_14 (
    .D(Datos_de_entrada), .en(Register_13_on_off), .Q(reg13_out), .clk(Clock), .clr(Reset));
  Register #(.width(32)) register_15 (
    .D(Datos_de_entrada), .en(Register_14_on_off), .Q(reg14_out), .clk(Clock), .clr(Reset));
  Register #(.width(32)) register_16 (
    .D(Datos_de_entrada), .en(Register_15_on_off), .Q(reg15_out), .clk(Clock), .clr(Reset));
  Register #(.width(32)) register_17 (
    .D(Datos_de_entrada), .en(Register_16_on_off), .Q(reg16_out), .clk(Clock), .clr(Reset));
  Register #(.width(32)) register_18 (
    .D(Datos_de_entrada), .en(Register_17_on_off), .Q(reg17_out), .clk(Clock), .clr(Reset));
  Register #(.width(32)) register_19 (
    .D(Datos_de_entrada), .en(Register_16_on_off), .Q(reg18_out), .clk(Clock), .clr(Reset));
  Register #(.width(32)) register_20 (
    .D(Datos_de_entrada), .en(Register_17_on_off), .Q(reg19_out), .clk(Clock), .clr(Reset));
  Register #(.width(32)) register_21 (
    .D(Datos_de_entrada), .en(Register_20_on_off), .Q(reg20_out), .clk(Clock), .clr(Reset));
  Register #(.width(32)) register_22 (
    .D(Datos_de_entrada), .en(Register_21_on_off), .Q(reg21_out), .clk(Clock), .clr(Reset));
  Register #(.width(32)) register_23 (
    .D(Datos_de_entrada), .en(Register_22_on_off), .Q(reg22_out), .clk(Clock), .clr(Reset));
  Register #(.width(32)) register_24 (
    .D(Datos_de_entrada), .en(Register_23_on_off), .Q(reg23_out), .clk(Clock), .clr(Reset));
  Register #(.width(32)) register_25 (
    .D(Datos_de_entrada), .en(Register_24_on_off), .Q(reg24_out), .clk(Clock), .clr(Reset));
  Register #(.width(32)) register_26 (
    .D(Datos_de_entrada), .en(Register_25_on_off), .Q(reg25_out), .clk(Clock), .clr(Reset));
  Register #(.width(32)) register_27 (
    .D(Datos_de_entrada), .en(Register_26_on_off), .Q(reg26_out), .clk(Clock), .clr(Reset));
  Register #(.width(32)) register_28 (
    .D(Datos_de_entrada), .en(Register_27_on_off), .Q(reg27_out), .clk(Clock), .clr(Reset));
  Register #(.width(32)) register_29 (
    .D(Datos_de_entrada), .en(Register_28_on_off), .Q(reg28_out), .clk(Clock), .clr(Reset));
  Register #(.width(32)) register_30 (
    .D(Datos_de_entrada), .en(Register_29_on_off), .Q(reg29_out), .clk(Clock), .clr(Reset));
  Register #(.width(32)) register_31 (
    .D(Datos_de_entrada), .en(Register_30_on_off), .Q(reg30_ut), .clk(Clock), .clr(Reset));
  Register #(.width(32)) register_32 (
    .D(Datos_de_entrada), .en(Register_31_on_off), .Q(reg31_out), .clk(Clock), .clr(Reset));
  Demultiplexer #(.select(5)) demultiplexer_1 (
    .out0(Register_0_on_off), .out1(Register_1_on_off), .out2(Register_2_on_off), .out3(Register_3_on_off),
    .out4(Register_4_on_off), .out5(Register_5_on_off), .out6(Register_6_on_off), .out7(Register_7_on_off),
    .out8(Register_8_on_off), .out9(Register_9_on_off), .out10(Register_10_on_off),
    .out11(Register_11_on_off), .out12(Register_12_on_off), .out13(Register_13_on_off),
    .out14(Register_14_on_off), .out15(Register_15_on_off), .out16(Register_16_on_off),
    .out17(Register_17_on_off), .out18(Register_18_on_off), .out19(Register_19_on_off),
    .out20(Register_20_on_off), .out21(Register_21_on_off), .out22(Register_22_on_off),
    .out23(Register_23_on_off), .out24(Register_24_on_off), .out25(Register_25_on_off),
    .out26(Register_26_on_off), .out27(Register_27_on_off), .out28(Register_28_on_off),
    .out29(Register_29_on_off), .out30(Register_30_on_off), .out31(Register_31_on_off), .in(Read_Write),
    .sel(\Dirección_de_destino ));  // open: en
  Multiplexer #(.select(5), .width(32)) multiplexer_1 (
    .in0(reg0_out), .in1(reg1_out), .in2(reg2_out), .in3(reg3_out), .in4(reg4_out), .in5(reg5_out),
    .in6(reg6_out), .in7(reg7_out), .in8(reg8_out), .in9(reg9_out), .in10(reg10_out), .in11(reg11_out),
    .in12(reg12_out), .in13(reg13_out), .in14(reg14_out), .in15(reg15_out), .in16(reg16_out),
    .in17(reg17_out), .in18(reg18_out), .in19(reg19_out), .in20(reg20_out), .in21(reg21_out),
    .in22(reg22_out), .in23(reg23_out), .in24(reg24_out), .in25(reg25_out), .in26(reg26_out),
    .in27(reg27_out), .in28(reg28_out), .in29(reg29_out), .in30(reg30_out), .in31(reg31_out),
    .out(Read_Data_1), .sel(Selector_de_salida_A));  // open: en
  Multiplexer #(.select(5), .width(32)) multiplexer_2 (
    .in0(reg0_out), .in1(reg1_out), .in2(reg2_out), .in3(reg3_out), .in4(reg4_out), .in5(reg5_out),
    .in6(reg6_out), .in7(reg7_out), .in8(reg8_out), .in9(reg9_out), .in10(reg10_out), .in11(reg11_out),
    .in12(reg12_out), .in13(reg13_out), .in14(reg14_out), .in15(reg15_out), .in16(reg16_out),
    .in17(reg17_out), .in18(reg18_out), .in19(reg19_out), .in20(reg20_out), .in21(reg21_out),
    .in22(reg22_out), .in23(reg23_out), .in24(reg24_out), .in25(reg25_out), .in26(reg26_out),
    .in27(reg27_out), .in28(reg28_out), .in29(reg29_out), .in30(reg30_out), .in31(reg31_out),
    .out(Read_Data_2), .sel(Selector_de_salida_B));  // open: en

  // Other names for the same wires on the sheet: clk = Clock; input_value[31:0] = Datos_de_entrada; R_W = Read_Write;
  //   read_dataA[31:0] = Read_Data_1; read_dataB[31:0] = Read_Data_2; read_regA[4:0] = Selector_de_salida_A;
  //   read_regB[4:0] = Selector_de_salida_B; write_reg[4:0] = \Dirección_de_destino 

  // Notes on the sheet:
  //   Inputs
  //   OUTPUTS from your circuit
endmodule

module DataPath (
  input  [31:0] in_1,
  input  Clock,
  input  [2:0] Instruction,
  output Overflow,
  output Neg,
  output Zero,
  output Carry
);

  wire instructiondecoder_1_read_write;
  wire [4:0] instructiondecoder_1_destination_address, instructiondecoder_1_selector_a,
       instructiondecoder_1_selector_b;
  wire [5:3] undriven;
  wire [31:0] instructiondecoder_1_destination_input, registerfile_1_read_data_1, registerfile_1_read_data_2;

  InstructionDecoder instructiondecoder_1 (
    .Instruction(in_1), .Destination_Address(instructiondecoder_1_destination_address),
    .Destination_Input(instructiondecoder_1_destination_input), .Read_Write(instructiondecoder_1_read_write),
    .Selector_A(instructiondecoder_1_selector_a), .Selector_B(instructiondecoder_1_selector_b));  // open: OpCode, Jump_Instruction, MemToReg, ALUOp, Offset, JumpAddress, ExtOp, ALUSrc
  RegisterFile registerfile_1 (
    .\Dirección_de_destino (instructiondecoder_1_destination_address),
    .Read_Write(instructiondecoder_1_read_write), .Datos_de_entrada(instructiondecoder_1_destination_input),
    .Selector_de_salida_A(instructiondecoder_1_selector_a),
    .Selector_de_salida_B(instructiondecoder_1_selector_b), .Clock(Clock),
    .Read_Data_1(registerfile_1_read_data_1), .Read_Data_2(registerfile_1_read_data_2));  // open: Reset
  ALU alu_1 (
    .Op1(registerfile_1_read_data_1), .Carry(Carry), .Zero(Zero), .Op2(registerfile_1_read_data_2),
    .Neg(Neg), .Overflow(Overflow), .Instruction({undriven, Instruction}));  // open: Auxiliar_Reg, Result
  // Pins of 3 and 6 bits meet at {undriven, Instruction}
endmodule

module ALU (
  input  [31:0] Op1,
  input  [31:0] Op2,
  input  [5:0] Instruction,
  output [31:0] Auxiliar_Reg,
  output [31:0] Result,
  output Carry,
  output Zero,
  output Neg,
  output Overflow
);

  wire adder_1_cout, and_2_out, and_3_out, and_4_out, and_5_out, and_6_out, and_7_out, comparator_1_eq,
       comparator_2_eq, subtractor_1_bout, xor_1_out, xor_2_out, xor_3_out, xor_4_out;
  wire [31:0] and_1_out, div, mult, multiplier_1_cout, not_1_out, not_2_out, or_1_out, reminder, sub, sum,
       undriven;

  Adder #(.width(32)) adder_1 (.a(Op1), .b(Op2), .out(sum), .cin(1'b0), .cout(adder_1_cout));
  Subtractor #(.width(32)) subtractor_1 (.a(Op1), .b(Op2), .out(sub), .bin(1'b0), .bout(subtractor_1_bout));
  Multiplier #(.width(32)) multiplier_1 (.a(Op1), .b(Op2), .out(mult), .cout(multiplier_1_cout));  // open: cin
  Divider #(.width(32)) divider_1 (.a(Op1), .b(Op2), .out(div), .upper(undriven), .rem(reminder));
  assign and_1_out = Op1 & Op2;  // AND_Gate and_1, 32 bits wide
  assign or_1_out = Op1 | Op2;  // OR_Gate or_1, 32 bits wide
  assign not_1_out = ~Op1;  // NOT_Gate not_1, 32 bits wide
  xor xor_1 (xor_1_out, Op1[31], sum[31]);
  xor xor_2 (xor_2_out, sum[31], Op2[31]);
  xor xor_3 (xor_3_out, Op1[31], sub[31]);
  xor xor_4 (xor_4_out, sub[31], Op2[31]);
  and and_2 (and_2_out, xor_1_out, xor_2_out);
  and and_3 (and_3_out, xor_3_out, xor_4_out);
  Comparator #(.width(3)) comparator_1 (.a(Instruction[2:0]), .b(3'b000), .eq(comparator_1_eq));  // open: gt, lt
  Comparator #(.width(3)) comparator_2 (.a(Instruction[2:0]), .b(3'b001), .eq(comparator_2_eq));  // open: gt, lt
  Multiplexer #(.select(3), .width(32), .enable("false")) multiplexer_1 (
    .in0({32{1'b0}}), .in1({32{1'b0}}), .in2(multiplier_1_cout), .in3(undriven), .in4({32{1'b0}}),
    .in5({32{1'b0}}), .in6({32{1'b0}}), .in7(not_2_out), .out(Auxiliar_Reg), .sel(Instruction[2:0]));
  assign not_2_out = ~Op2;  // NOT_Gate not_2, 32 bits wide
  Multiplexer #(.select(3), .width(32), .enable("false")) multiplexer_2 (
    .in0(sum), .in1(sub), .in2(mult), .in3(div), .in4(reminder), .in5(and_1_out), .in6(or_1_out),
    .in7(not_1_out), .out(Result), .sel(Instruction[2:0]));
  and and_4 (and_4_out, and_2_out, comparator_1_eq);
  and and_5 (and_5_out, comparator_1_eq, adder_1_cout);
  or or_2 (Carry, and_5_out, and_6_out);
  and and_6 (and_6_out, subtractor_1_bout, comparator_2_eq);
  and and_7 (and_7_out, comparator_2_eq, and_3_out);
  Comparator #(.width(32)) comparator_3 (.a(Result), .b({32{1'b0}}), .eq(Zero), .lt(Neg));  // open: gt
  or or_3 (Overflow, and_4_out, and_7_out);
  // Pins of 3 and 6 bits meet at Instruction

  // Other names for the same wires on the sheet: auxiliar[31:0] = Auxiliar_Reg; opA[31:0] = Op1; opB[31:0] = Op2;
  //   Overflow_flag = Overflow; S[5:0] = Instruction

  // Notes on the sheet:
  //   INPUTS
  //   Outputs
  //   Flags
endmodule

module BranchControl (
  input  [31:0] Instruction_Address,
  input  [31:0] Jump_Size,
  input  Jump,
  input  Flag_Condition,
  output [31:0] Next_Instruction_Address
);

  wire and_1_out;
  wire [31:0] adder_1_out;

  Adder #(.width(32)) adder_1 (.a(Instruction_Address), .b(Jump_Size), .out(adder_1_out));  // open: cin, cout
  and and_1 (and_1_out, Jump, Flag_Condition);
  Multiplexer #(.width(32), .enable("false")) multiplexer_1 (
    .in0(Instruction_Address), .in1(adder_1_out), .out(Next_Instruction_Address), .sel(and_1_out));
endmodule

module InstructionDecoder (
  input  [31:0] Instruction,
  output [5:0] OpCode,
  output [4:0] Destination_Address,
  output [31:0] Destination_Input,
  output Read_Write,
  output [4:0] Selector_A,
  output [4:0] Selector_B,
  output Jump_Instruction,
  output MemToReg,
  output [5:0] ALUOp,
  output [15:0] Offset,
  output [25:0] JumpAddress,
  output ExtOp,
  output ALUSrc
);

  wire add_out, and_out, andi_out, beq_out, bgtz_out, blez_out, bltz_out, bne_out, buffer_1_out,
       comparator_1_eq, comparator_2_eq, comparator_3_eq, comparator_4_eq, comparator_5_eq, comparator_6_eq,
       comparator_7_eq, comparator_8_eq, comparator_9_eq, comparator_10_eq, comparator_11_eq,
       comparator_12_eq, comparator_13_eq, comparator_14_eq, comparator_16_eq, comparator_17_eq,
       comparator_18_eq, comparator_19_eq, comparator_20_eq, comparator_21_eq, comparator_22_eq,
       comparator_23_eq, comparator_24_eq, comparator_25_eq, comparator_26_eq, comparator_27_eq,
       comparator_28_eq, comparator_29_eq, comparator_30_eq, comparator_31_eq, comparator_32_eq,
       comparator_33_eq, div_out, divu_out, j_out, mfhi_out, mflo_out, mult_out, multu_out, nop_out, nor_out,
       or_out, ori_out, pop_out, push_pop_out, RegDest, slt_out, slti_out, sltiu_out, sltu_out, sub_out,
       xor_out, xori_out;

  Comparator #(.width(6)) comparator_1 (.a(Instruction[31:26]), .b(6'b101011), .eq(comparator_1_eq));  // open: gt, lt
  Comparator #(.width(6)) comparator_2 (.a(Instruction[31:26]), .b(6'b100011), .eq(comparator_2_eq));  // open: gt, lt
  Comparator #(.width(6)) comparator_3 (.a(Instruction[31:26]), .b(6'b001110), .eq(comparator_3_eq));  // open: gt, lt
  Comparator #(.width(6)) comparator_4 (.a(Instruction[31:26]), .b(6'b001101), .eq(comparator_4_eq));  // open: gt, lt
  Comparator #(.width(6)) comparator_5 (.a(Instruction[31:26]), .b(6'b001100), .eq(comparator_5_eq));  // open: gt, lt
  Comparator #(.width(6)) comparator_6 (.a(Instruction[31:26]), .b(6'b001011), .eq(comparator_6_eq));  // open: gt, lt
  Comparator #(.width(6)) comparator_7 (.a(Instruction[31:26]), .b(6'b001010), .eq(comparator_7_eq));  // open: gt, lt
  Comparator #(.width(6)) comparator_8 (.a(Instruction[31:26]), .b(6'b001000), .eq(comparator_8_eq));  // open: gt, lt
  Comparator #(.width(6)) comparator_9 (.a(Instruction[31:26]), .b(6'b000111), .eq(comparator_9_eq));  // open: gt, lt
  Comparator #(.width(6)) comparator_10 (.a(Instruction[31:26]), .b(6'b000110), .eq(comparator_10_eq));  // open: gt, lt
  Comparator #(.width(6)) comparator_11 (.a(Instruction[31:26]), .b(6'b000101), .eq(comparator_11_eq));  // open: gt, lt
  Comparator #(.width(6)) comparator_12 (.a(Instruction[31:26]), .b(6'b000100), .eq(comparator_12_eq));  // open: gt, lt
  Comparator #(.width(6)) comparator_13 (.a(Instruction[31:26]), .b(6'b000010), .eq(comparator_13_eq));  // open: gt, lt
  Comparator #(.width(6)) comparator_14 (.a(Instruction[31:26]), .b(6'b000001), .eq(comparator_14_eq));  // open: gt, lt
  Comparator #(.width(6)) comparator_15 (.a(Instruction[31:26]), .b({6{1'b0}}), .eq(RegDest));  // open: gt, lt
  Comparator #(.width(6)) comparator_16 (.a(Instruction[31:26]), .b(6'b111000), .eq(comparator_16_eq));  // open: gt, lt
  Comparator #(.width(6)) comparator_17 (.a(Instruction[5:0]), .b(6'b100000), .eq(comparator_17_eq));  // open: gt, lt
  Comparator #(.width(6)) comparator_18 (.a(Instruction[5:0]), .b(6'b100010), .eq(comparator_18_eq));  // open: gt, lt
  Comparator #(.width(6)) comparator_19 (.a(Instruction[5:0]), .b(6'b011000), .eq(comparator_19_eq));  // open: gt, lt
  Comparator #(.width(6)) comparator_20 (.a(Instruction[5:0]), .b(6'b011001), .eq(comparator_20_eq));  // open: gt, lt
  Comparator #(.width(6)) comparator_21 (.a(Instruction[5:0]), .b(6'b011010), .eq(comparator_21_eq));  // open: gt, lt
  Comparator #(.width(6)) comparator_22 (.a(Instruction[5:0]), .b(6'b011011), .eq(comparator_22_eq));  // open: gt, lt
  Comparator #(.width(6)) comparator_23 (.a(Instruction[5:0]), .b(6'b100100), .eq(comparator_23_eq));  // open: gt, lt
  Comparator #(.width(6)) comparator_24 (.a(Instruction[5:0]), .b(6'b100101), .eq(comparator_24_eq));  // open: gt, lt
  Comparator #(.width(6)) comparator_25 (.a(Instruction[5:0]), .b(6'b100111), .eq(comparator_25_eq));  // open: gt, lt
  Comparator #(.width(6)) comparator_26 (.a(Instruction[5:0]), .b(6'b101000), .eq(comparator_26_eq));  // open: gt, lt
  Comparator #(.width(6)) comparator_27 (.a(Instruction[5:0]), .b(6'b101010), .eq(comparator_27_eq));  // open: gt, lt
  Comparator #(.width(6)) comparator_28 (.a(Instruction[5:0]), .b(6'b101011), .eq(comparator_28_eq));  // open: gt, lt
  Comparator #(.width(6)) comparator_29 (.a(Instruction[5:0]), .b(6'b010000), .eq(comparator_29_eq));  // open: gt, lt
  Comparator #(.width(6)) comparator_30 (.a(Instruction[5:0]), .b(6'b010010), .eq(comparator_30_eq));  // open: gt, lt
  Comparator #(.width(6)) comparator_31 (.a(Instruction[5:0]), .b({6{1'b0}}), .eq(comparator_31_eq));  // open: gt, lt
  // Buffer sw has open pins: in=comparator_1_eq, out=open
  buf lw (MemToReg, comparator_2_eq);
  buf xori (xori_out, comparator_3_eq);
  buf ori (ori_out, comparator_4_eq);
  buf andi (andi_out, comparator_5_eq);
  buf sltiu (sltiu_out, comparator_6_eq);
  buf slti (slti_out, comparator_7_eq);
  buf buffer_1 (buffer_1_out, comparator_8_eq);
  buf bgtz (bgtz_out, comparator_9_eq);
  buf blez (blez_out, comparator_10_eq);
  buf bne (bne_out, comparator_11_eq);
  buf beq (beq_out, comparator_12_eq);
  buf j (j_out, comparator_13_eq);
  buf bltz (bltz_out, comparator_14_eq);
  buf push_pop (push_pop_out, comparator_16_eq);
  and add (add_out, RegDest, comparator_17_eq);
  and sub (sub_out, RegDest, comparator_18_eq);
  and mult (mult_out, RegDest, comparator_19_eq);
  and multu (multu_out, RegDest, comparator_20_eq);
  and div (div_out, RegDest, comparator_21_eq);
  and divu (divu_out, RegDest, comparator_22_eq);
  and \and  (and_out, RegDest, comparator_23_eq);
  and \or  (or_out, RegDest, comparator_24_eq);
  and \nor  (nor_out, RegDest, comparator_25_eq);
  and \xor  (xor_out, RegDest, comparator_26_eq);
  and slt (slt_out, RegDest, comparator_27_eq);
  and sltu (sltu_out, RegDest, comparator_28_eq);
  and mfhi (mfhi_out, RegDest, comparator_29_eq);
  and mflo (mflo_out, RegDest, comparator_30_eq);
  and nop (nop_out, RegDest, comparator_31_eq);
  nor nor_2 (ExtOp, xori_out, ori_out, andi_out);
  or or_2 (Jump_Instruction, bgtz_out, blez_out, bne_out, beq_out, j_out, bltz_out);
  and pop (pop_out, push_pop_out, comparator_32_eq);
  Comparator #(.width(6)) comparator_32 (.a(Instruction[5:0]), .b({6{1'b0}}), .eq(comparator_32_eq));  // open: gt, lt
  // AND_Gate push has open pins: in0=push_pop_out, in1=comparator_33_eq, out=open
  Comparator #(.width(6)) comparator_33 (.a(Instruction[5:0]), .b(6'b000001), .eq(comparator_33_eq));  // open: gt, lt
  or or_3 (Read_Write, MemToReg, xori_out, ori_out, andi_out, sltiu_out, slti_out, buffer_1_out, RegDest, pop_out);
  nor nor_3 (ALUSrc, Jump_Instruction, RegDest);
  Multiplexer #(.width(5), .enable("false")) multiplexer_1 (
    .in0(Instruction[20:16]), .in1(Instruction[15:11]), .out(Destination_Address), .sel(RegDest));

  assign ALUOp = Instruction[5:0];
  assign JumpAddress = Instruction[25:0];
  assign Offset = Instruction[15:0];
  assign OpCode = Instruction[31:26];
  assign Selector_A = Instruction[25:21];
  assign Selector_B = Instruction[20:16];

  // Other names for the same wires on the sheet: alu_src = ALUSrc; ext_op = ExtOp; address[25:0] = Instruction[25:0];
  //   func_code[5:0] = Instruction[5:0]; Params[19:0] = Instruction[25:6]; write_address_R[4:0] = Instruction[15:11];
  //   operand_2[4:0] = Instruction[20:16]; write_address_I[4:0] = Instruction[20:16];
  //   operand_1[4:0] = Instruction[25:21]; op_code[5:0] = Instruction[31:26]; mem_to_reg = MemToReg;
  //   write_address[4:0] = Destination_Address

  // Notes on the sheet:
  //   addi
endmodule

module ControlUnit (
  input  [5:0] Opcode,
  input  [5:0] FuncCode,
  output MemToReg,
  output [3:0] ALUOp,
  output RegWrite,
  output Jump,
  output BNE,
  output ExtOp,
  output BEQ,
  output MemWrite,
  output MemRead,
  output ALUSrc
);

  wire andi_out, beq_out, bgtz_out, blez_out, bltz_out, bne_out, buffer_1_out, comparator_1_eq,
       comparator_2_eq, comparator_3_eq, comparator_4_eq, comparator_5_eq, comparator_6_eq, comparator_7_eq,
       comparator_8_eq, comparator_9_eq, comparator_10_eq, comparator_11_eq, comparator_12_eq,
       comparator_13_eq, comparator_14_eq, comparator_15_eq, comparator_16_eq, comparator_17_eq,
       comparator_18_eq, comparator_19_eq, comparator_20_eq, j_out, ori_out, pop_out, push_pop_out,
       R_type_out, slti_out, sltiu_out, undriven_2, xori_out;
  wire [5:0] undriven;

  // Buffer sw has open pins: in=comparator_1_eq, out=open
  Comparator #(.width(6)) comparator_1 (.a(Opcode), .b(6'b101011), .eq(comparator_1_eq));  // open: gt, lt
  buf lw (MemToReg, comparator_2_eq);
  Comparator #(.width(6)) comparator_2 (.a(Opcode), .b(6'b100011), .eq(comparator_2_eq));  // open: gt, lt
  Comparator #(.width(6)) comparator_3 (.a(Opcode), .b(6'b001110), .eq(comparator_3_eq));  // open: gt, lt
  buf xori (xori_out, comparator_3_eq);
  buf ori (ori_out, comparator_4_eq);
  Comparator #(.width(6)) comparator_4 (.a(Opcode), .b(6'b001101), .eq(comparator_4_eq));  // open: gt, lt
  Comparator #(.width(6)) comparator_5 (.a(Opcode), .b(6'b001100), .eq(comparator_5_eq));  // open: gt, lt
  buf andi (andi_out, comparator_5_eq);
  buf sltiu (sltiu_out, comparator_6_eq);
  Comparator #(.width(6)) comparator_6 (.a(Opcode), .b(6'b001011), .eq(comparator_6_eq));  // open: gt, lt
  buf slti (slti_out, comparator_7_eq);
  Comparator #(.width(6)) comparator_7 (.a(Opcode), .b(6'b001010), .eq(comparator_7_eq));  // open: gt, lt
  Comparator #(.width(6)) comparator_8 (.a(Opcode), .b(6'b001000), .eq(comparator_8_eq));  // open: gt, lt
  buf buffer_1 (buffer_1_out, comparator_8_eq);
  buf bgtz (bgtz_out, comparator_9_eq);
  Comparator #(.width(6)) comparator_9 (.a(Opcode), .b(6'b000111), .eq(comparator_9_eq));  // open: gt, lt
  buf blez (blez_out, comparator_10_eq);
  Comparator #(.width(6)) comparator_10 (.a(Opcode), .b(6'b000110), .eq(comparator_10_eq));  // open: gt, lt
  Comparator #(.width(6)) comparator_11 (.a(Opcode), .b(6'b000101), .eq(comparator_11_eq));  // open: gt, lt
  buf u_bne (bne_out, comparator_11_eq);
  buf u_beq (beq_out, comparator_12_eq);
  Comparator #(.width(6)) comparator_12 (.a(Opcode), .b(6'b000100), .eq(comparator_12_eq));  // open: gt, lt
  buf j (j_out, comparator_13_eq);
  Comparator #(.width(6)) comparator_13 (.a(Opcode), .b(6'b000010), .eq(comparator_13_eq));  // open: gt, lt
  Comparator #(.width(6)) comparator_14 (.a(Opcode), .b(6'b000001), .eq(comparator_14_eq));  // open: gt, lt
  buf bltz (bltz_out, comparator_14_eq);
  Comparator #(.width(6)) comparator_15 (.a(Opcode), .b({6{1'b0}}), .eq(comparator_15_eq));  // open: gt, lt
  buf R_type (R_type_out, comparator_15_eq);
  Comparator #(.width(6)) comparator_16 (.a(Opcode), .b(6'b111000), .eq(comparator_16_eq));  // open: gt, lt
  buf push_pop (push_pop_out, comparator_16_eq);
  Comparator #(.width(6)) comparator_17 (.a(FuncCode), .b({6{1'b0}}), .eq(comparator_17_eq));  // open: gt, lt
  Comparator #(.width(6)) comparator_18 (.a(FuncCode), .b(6'b000001), .eq(comparator_18_eq));  // open: gt, lt
  Comparator #(.width(6)) comparator_19 (.a(undriven), .b(6'b010010), .eq(comparator_19_eq));  // open: gt, lt
  Comparator #(.width(6)) comparator_20 (.a(undriven), .b({6{1'b0}}), .eq(comparator_20_eq));  // open: gt, lt
  and pop (pop_out, push_pop_out, comparator_17_eq);
  // AND_Gate push has open pins: in0=push_pop_out, in1=comparator_18_eq, out=open
  // AND_Gate mflo has open pins: in0=undriven_2, in1=comparator_19_eq, out=open
  // AND_Gate nop has open pins: in0=undriven_2, in1=comparator_20_eq, out=open
  or or_1 (RegWrite, MemToReg, xori_out, ori_out, andi_out, sltiu_out, slti_out, buffer_1_out, R_type_out, pop_out);
  nor nor_1 (ExtOp, xori_out, ori_out, andi_out);
  nor nor_2 (ALUSrc, bgtz_out, bne_out, blez_out, beq_out, bltz_out, R_type_out);

  // Notes on the sheet:
  //   addi
endmodule

module CPU (
  input  Kbd_Available,
  input  [6:0] Kbd_ASCII_Data,
  input  [31:0] RAM_Out_0,
  input  [31:0] RAM_Out_1,
  input  Reset,
  input  [31:0] RAM_Out_2,
  input  Clock,
  input  [31:0] RAM_Out_3,
  input  [31:0] Instruction,
  input  [3:0] Read_Time,
  input  [3:0] Write_Time,
  output Kbd_Enable,
  output [15:0] Address,
  output Kbd_Clear,
  output TTY_Enable,
  output [6:0] TTY_ASCII_Data,
  output Stop,
  output [31:0] RAM_In_0,
  output [31:0] RAM_In_1,
  output [31:0] RAM_In_2,
  output [31:0] RAM_In_3,
  output [3:0] Mask,
  output nRead_Write,
  output Chip_Select
);

  wire clk_out, controlunit_1_alusrc, controlunit_1_extop, ExtOp, instructiondecoder_1_read_write;
  wire [4:0] instructiondecoder_1_destination_address, instructiondecoder_1_selector_a,
       instructiondecoder_1_selector_b;
  wire [5:0] instructiondecoder_1_aluop, instructiondecoder_1_opcode, undriven;
  wire [15:0] instructiondecoder_1_offset;
  wire [31:0] extender_1_out_3, instructiondecoder_1_destination_input, multiplexer_1_out,
       registerfile_1_read_data_1, registerfile_1_read_data_2;

  Clock clk (.out(clk_out));
  // Probe on instructiondecoder_1_selector_a
  // Probe on instructiondecoder_1_selector_b
  InstructionDecoder instructiondecoder_1 (
    .Instruction(Instruction), .OpCode(instructiondecoder_1_opcode),
    .Destination_Address(instructiondecoder_1_destination_address),
    .Destination_Input(instructiondecoder_1_destination_input), .Read_Write(instructiondecoder_1_read_write),
    .Selector_A(instructiondecoder_1_selector_a), .Selector_B(instructiondecoder_1_selector_b),
    .ALUOp(instructiondecoder_1_aluop), .Offset(instructiondecoder_1_offset), .ExtOp(ExtOp));  // open: Jump_Instruction, MemToReg, JumpAddress, ALUSrc
  ControlUnit controlunit_1 (
    .Opcode(instructiondecoder_1_opcode), .FuncCode(undriven), .ExtOp(controlunit_1_extop),
    .ALUSrc(controlunit_1_alusrc));  // open: MemToReg, ALUOp, RegWrite, Jump, BNE, BEQ, MemWrite, MemRead
  // Probe on registerfile_1_read_data_1
  // Probe on registerfile_1_read_data_2
  Extender extender_1 (.Input(instructiondecoder_1_offset), .ExtOp(ExtOp), .out_3(extender_1_out_3));
  RegisterFile registerfile_1 (
    .\Dirección_de_destino (instructiondecoder_1_destination_address),
    .Read_Write(instructiondecoder_1_read_write), .Datos_de_entrada(instructiondecoder_1_destination_input),
    .Selector_de_salida_A(instructiondecoder_1_selector_a),
    .Selector_de_salida_B(instructiondecoder_1_selector_b), .Clock(clk_out),
    .Read_Data_1(registerfile_1_read_data_1), .Read_Data_2(registerfile_1_read_data_2));  // open: Reset
  Multiplexer #(.width(32), .enable("false")) multiplexer_1 (
    .in0(registerfile_1_read_data_2), .in1(extender_1_out_3), .out(multiplexer_1_out),
    .sel(controlunit_1_alusrc));
  // Probe on RAM_Out_0
  ALU alu_1 (
    .Op1(registerfile_1_read_data_1), .Result(RAM_Out_0), .Op2(multiplexer_1_out));  // open: Auxiliar_Reg, Carry, Zero, Neg, Overflow, Instruction

  assign Address = {16{1'b0}};
  assign Chip_Select = 1'b0;
  assign Kbd_Clear = 1'b0;
  assign Kbd_Enable = 1'b1;
  assign Mask = 4'b0000;
  assign nRead_Write = 1'b0;
  assign RAM_In_0 = {32{1'b0}};
  assign RAM_In_1 = {32{1'b0}};
  assign RAM_In_2 = {32{1'b0}};
  assign RAM_In_3 = {32{1'b0}};
  assign Stop = 1'b0;
  assign TTY_Enable = 1'b0;

  // Other names for the same wires on the sheet: CLK = Clock; CLR = Reset; KBD_AVAIL = Kbd_Available;
  //   KBD_DATA[6:0] = Kbd_ASCII_Data; RAM_OUTPUT_0[31:0] = RAM_Out_0; RAM_OUTPUT_1[31:0] = RAM_Out_1;
  //   RAM_OUTPUT_2[31:0] = RAM_Out_2; RAM_OUTPUT_3[31:0] = RAM_Out_3; TTY_DATA[6:0] = TTY_ASCII_Data

  // Notes on the sheet:
  //   RAM ADDRESS
  //   DATA FROM RAM
  //   DATA TO RAM
  //   DATA WRITE MASK
  //   RAM TIMING
  //   RAM CONTROL
  //   KEYBOARD
  //   TTY
  //   SEQUENCING
  //   Esto lo tienen que borrar:
endmodule

module Extender (
  input  [15:0] Input,
  input  ExtOp,
  output [31:0] out_3
);

  wire [31:0] bit_extender_1_out, bit_extender_2_out;

  assign bit_extender_1_out = {{16{1'b0}}, Input};  // Bit_Extender bit_extender_1
  assign bit_extender_2_out = {{16{Input[15]}}, Input};  // Bit_Extender bit_extender_2
  Multiplexer #(.width(32), .enable("false")) multiplexer_1 (
    .in0(bit_extender_1_out), .in1(bit_extender_2_out), .out(out_3), .sel(ExtOp));
endmodule

module ALU2 (
  input  [31:0] Op1,
  input  [31:0] Op2,
  input  [5:0] Instruction,
  output [31:0] HI,
  output [31:0] LO,
  output [31:0] Output
);

  wire adder_1_cout, and_1_out, and_2_out, and_3_out, and_4_out, and_5_out, and_6_out, Carry,
       comparator_1_eq, comparator_2_eq, decoder_1_out4, decoder_1_out6, decoder_1_out7, is_div, is_divu,
       is_mult, is_multu, multiplexer_4_p7, not_1_out, not_2_out, not_4_out, Overflow_flag,
       subtractor_1_bout, xor_1_out, xor_2_out, xor_3_out, xor_4_out;
  wire [31:0] auxiliar, divu_hi, divu_lo, mult_hi, mult_lo, multiplexer_1_out, multiplexer_2_out, multu_hi,
       multu_lo, not_3_out, sub, sum;

  not not_1 (not_1_out, Instruction[5]);
  Decoder #(.select(5), .disabled(0)) decoder_1 (
    .out4(decoder_1_out4), .out6(decoder_1_out6), .out7(decoder_1_out7), .out24(is_mult), .out25(is_multu),
    .out26(is_divu), .out27(is_div), .sel(Instruction[4:0]), .en(not_1_out));  // open: out0, out1, out2, out3, out5, out8, out9, out10, out11, out12, out13, out14, out15, out16, out17, out18, out19, out20, out21, out22, out23, out28, out29, out30, out31
  Adder #(.width(32)) adder_1 (.a(Op1), .b(Op2), .out(sum), .cin(1'b0), .cout(adder_1_cout));
  Subtractor #(.width(32)) subtractor_1 (.a(Op1), .b(Op2), .out(sub), .bin(1'b0), .bout(subtractor_1_bout));
  // Probe on Op1
  // Probe on Op2
  xor xor_1 (xor_1_out, Op1[31], sum[31]);
  xor xor_2 (xor_2_out, sum[31], Op2[31]);
  xor xor_3 (xor_3_out, Op1[31], sub[31]);
  xor xor_4 (xor_4_out, sub[31], Op2[31]);
  and and_1 (and_1_out, xor_1_out, xor_2_out);
  and and_2 (and_2_out, xor_3_out, xor_4_out);
  Comparator #(.width(6)) comparator_1 (.a(Instruction), .b(6'b100000), .eq(comparator_1_eq));  // open: gt, lt
  Comparator #(.width(6)) comparator_2 (.a(Instruction), .b(6'b100010), .eq(comparator_2_eq));  // open: gt, lt
  and and_3 (and_3_out, and_1_out, comparator_1_eq);
  and and_4 (and_4_out, comparator_1_eq, adder_1_cout);
  or or_1 (Carry, and_4_out, and_5_out);
  and and_5 (and_5_out, subtractor_1_bout, comparator_2_eq);
  and and_6 (and_6_out, comparator_2_eq, and_2_out);
  or or_2 (Overflow_flag, and_3_out, and_6_out);
  not not_2 (not_2_out, Instruction[5]);
  Multiplexer #(.select(5), .width(32)) multiplexer_1 (
    .in0(sum), .in2(sub), .out(multiplexer_1_out), .sel(Instruction[4:0]), .en(Instruction[5]));  // open: in1, in3, in4, in5, in6, in7, in8, in9, in10, in11, in12, in13, in14, in15, in16, in17, in18, in19, in20, in21, in22, in23, in24, in25, in26, in27, in28, in29, in30, in31
  Multiplexer #(.select(5), .width(32)) multiplexer_2 (
    .out(multiplexer_2_out), .sel(Instruction[4:0]), .en(not_2_out));  // open: in0, in1, in2, in3, in4, in5, in6, in7, in8, in9, in10, in11, in12, in13, in14, in15, in16, in17, in18, in19, in20, in21, in22, in23, in24, in25, in26, in27, in28, in29, in30, in31
  Multiplexer #(.width(32)) multiplexer_3 (
    .in0(multiplexer_1_out), .in1(multiplexer_2_out), .out(Output), .sel(not_2_out));  // open: en
  Multiplier #(.width(32)) multiplier_1 (.a(Op1), .b(Op2), .out(mult_lo), .cout(mult_hi));  // open: cin
  Divider #(.width(32)) divider_1 (.a(Op1), .b(Op2), .out(divu_lo), .rem(divu_hi));  // open: upper
  UnsignedMultiplier unsignedmultiplier_1 (.A(Op1), .B(Op2), .Low(multu_lo), .Hi(multu_hi));
  assign HI = is_multu ? multu_hi : 32'bz;  // Controlled_Buffer controlled_buffer_1
  assign HI = is_mult ? mult_hi : 32'bz;  // Controlled_Buffer controlled_buffer_2
  assign HI = is_divu ? divu_hi : 32'bz;  // Controlled_Buffer controlled_buffer_3
  assign LO = is_divu ? divu_lo : 32'bz;  // Controlled_Buffer controlled_buffer_4
  assign LO = is_mult ? mult_lo : 32'bz;  // Controlled_Buffer controlled_buffer_5
  assign LO = is_multu ? multu_lo : 32'bz;  // Controlled_Buffer controlled_buffer_6
  assign not_3_out = ~Op2;  // NOT_Gate not_3, 32 bits wide
  not not_4 (not_4_out, Instruction[5]);
  // Probe on HI
  // Probe on LO
  // Multiplexer #(.select(5), .width(32)) multiplexer_4: pin names not known; wires that end beside it: {32{1'b0}}, {32{1'b0}}, {32{1'b0}}, {32{1'b0}}, {32{1'b0}}, not_3_out, multiplexer_4_p7, multiplexer_4_p7, Instruction[4:0], not_4_out, auxiliar

  // Other names for the same wires on the sheet: opA[31:0] = Op1; opB[31:0] = Op2; S[5:0] = Instruction

  // Notes on the sheet:
  //   INPUTS
endmodule

module UnsignedMultiplier (
  input  [31:0] A,
  input  [31:0] B,
  output [31:0] Low,
  output [31:0] Hi
);

  wire [31:0] umultaux_1_output, umultaux_2_output, umultaux_3_output, umultaux_4_output, umultaux_5_output,
       umultaux_6_output, umultaux_7_output, umultaux_8_output, umultaux_9_output, umultaux_10_output,
       umultaux_11_output, umultaux_12_output, umultaux_13_output, umultaux_14_output, umultaux_15_output,
       umultaux_16_output, umultaux_17_output, umultaux_18_output, umultaux_19_output, umultaux_20_output,
       umultaux_21_output, umultaux_22_output, umultaux_23_output, umultaux_24_output, umultaux_25_output,
       umultaux_26_output, umultaux_27_output, umultaux_28_output, umultaux_29_output, umultaux_30_output,
       umultaux_31_output;

  // Probe on B
  // Probe on B
  // Probe on A
  // Probe on A
  UMultAux umultaux_1 (.A(A), .in_2(B[0]), .Last(Low[0]), .Prev({32{1'b0}}), .Output(umultaux_1_output));
  UMultAux umultaux_2 (.A(A), .in_2(B[1]), .Last(Low[1]), .Prev(umultaux_1_output), .Output(umultaux_2_output));
  UMultAux umultaux_3 (.A(A), .in_2(B[2]), .Last(Low[2]), .Prev(umultaux_2_output), .Output(umultaux_3_output));
  UMultAux umultaux_4 (.A(A), .in_2(B[3]), .Last(Low[3]), .Prev(umultaux_3_output), .Output(umultaux_4_output));
  UMultAux umultaux_5 (.A(A), .in_2(B[4]), .Last(Low[4]), .Prev(umultaux_4_output), .Output(umultaux_5_output));
  UMultAux umultaux_6 (.A(A), .in_2(B[5]), .Last(Low[5]), .Prev(umultaux_5_output), .Output(umultaux_6_output));
  UMultAux umultaux_7 (.A(A), .in_2(B[6]), .Last(Low[6]), .Prev(umultaux_6_output), .Output(umultaux_7_output));
  UMultAux umultaux_8 (.A(A), .in_2(B[7]), .Last(Low[7]), .Prev(umultaux_7_output), .Output(umultaux_8_output));
  UMultAux umultaux_9 (.A(A), .in_2(B[8]), .Last(Low[8]), .Prev(umultaux_8_output), .Output(umultaux_9_output));
  UMultAux umultaux_10 (.A(A), .in_2(B[9]), .Last(Low[9]), .Prev(umultaux_9_output), .Output(umultaux_10_output));
  UMultAux umultaux_11 (.A(A), .in_2(B[10]), .Last(Low[10]), .Prev(umultaux_10_output), .Output(umultaux_11_output));
  UMultAux umultaux_12 (.A(A), .in_2(B[11]), .Last(Low[11]), .Prev(umultaux_11_output), .Output(umultaux_12_output));
  UMultAux umultaux_13 (.A(A), .in_2(B[12]), .Last(Low[12]), .Prev(umultaux_12_output), .Output(umultaux_13_output));
  UMultAux umultaux_14 (.A(A), .in_2(B[13]), .Last(Low[13]), .Prev(umultaux_13_output), .Output(umultaux_14_output));
  UMultAux umultaux_15 (.A(A), .in_2(B[14]), .Last(Low[14]), .Prev(umultaux_14_output), .Output(umultaux_15_output));
  UMultAux umultaux_16 (.A(A), .in_2(B[15]), .Last(Low[15]), .Prev(umultaux_15_output), .Output(umultaux_16_output));
  UMultAux umultaux_17 (.A(A), .in_2(B[16]), .Last(Low[16]), .Prev(umultaux_16_output), .Output(umultaux_17_output));
  UMultAux umultaux_18 (.A(A), .in_2(B[17]), .Last(Low[17]), .Prev(umultaux_17_output), .Output(umultaux_18_output));
  UMultAux umultaux_19 (.A(A), .in_2(B[18]), .Last(Low[18]), .Prev(umultaux_18_output), .Output(umultaux_19_output));
  UMultAux umultaux_20 (.A(A), .in_2(B[19]), .Last(Low[19]), .Prev(umultaux_19_output), .Output(umultaux_20_output));
  UMultAux umultaux_21 (.A(A), .in_2(B[20]), .Last(Low[20]), .Prev(umultaux_20_output), .Output(umultaux_21_output));
  UMultAux umultaux_22 (.A(A), .in_2(B[21]), .Last(Low[21]), .Prev(umultaux_21_output), .Output(umultaux_22_output));
  UMultAux umultaux_23 (.A(A), .in_2(B[22]), .Last(Low[22]), .Prev(umultaux_22_output), .Output(umultaux_23_output));
  UMultAux umultaux_24 (.A(A), .in_2(B[23]), .Last(Low[23]), .Prev(umultaux_23_output), .Output(umultaux_24_output));
  UMultAux umultaux_25 (.A(A), .in_2(B[24]), .Last(Low[24]), .Prev(umultaux_24_output), .Output(umultaux_25_output));
  UMultAux umultaux_26 (.A(A), .in_2(B[25]), .Last(Low[25]), .Prev(umultaux_25_output), .Output(umultaux_26_output));
  UMultAux umultaux_27 (.A(A), .in_2(B[26]), .Last(Low[26]), .Prev(umultaux_26_output), .Output(umultaux_27_output));
  UMultAux umultaux_28 (.A(A), .in_2(B[27]), .Last(Low[27]), .Prev(umultaux_27_output), .Output(umultaux_28_output));
  UMultAux umultaux_29 (.A(A), .in_2(B[28]), .Last(Low[28]), .Prev(umultaux_28_output), .Output(umultaux_29_output));
  UMultAux umultaux_30 (.A(A), .in_2(B[29]), .Last(Low[29]), .Prev(umultaux_29_output), .Output(umultaux_30_output));
  UMultAux umultaux_31 (.A(A), .in_2(B[30]), .Last(Low[30]), .Prev(umultaux_30_output), .Output(umultaux_31_output));
  UMultAux umultaux_32 (.A(A), .in_2(B[31]), .Last(Low[31]), .Prev(umultaux_31_output), .Output(Hi));
  // Probe on Low
  // Probe on Low
  // Probe on Hi
  // Probe on Hi
endmodule

module UMultAux (
  input  [31:0] A,
  input  in_2,
  input  [31:0] Prev,
  output Last,
  output [31:0] Output
);

  wire [31:0] and_32_out;

  and and_1 (and_32_out[31], in_2, A[31]);
  and and_2 (and_32_out[30], in_2, A[30]);
  and and_3 (and_32_out[27], in_2, A[27]);
  and and_4 (and_32_out[29], in_2, A[29]);
  and and_5 (and_32_out[28], in_2, A[28]);
  and and_6 (and_32_out[25], in_2, A[25]);
  and and_7 (and_32_out[26], in_2, A[26]);
  and and_8 (and_32_out[23], in_2, A[23]);
  and and_9 (and_32_out[22], in_2, A[22]);
  and and_10 (and_32_out[24], in_2, A[24]);
  and and_11 (and_32_out[21], in_2, A[21]);
  and and_12 (and_32_out[19], in_2, A[19]);
  and and_13 (and_32_out[20], in_2, A[20]);
  and and_14 (and_32_out[18], in_2, A[18]);
  and and_15 (and_32_out[17], in_2, A[17]);
  and and_16 (and_32_out[15], in_2, A[15]);
  and and_17 (and_32_out[16], in_2, A[16]);
  and and_18 (and_32_out[14], in_2, A[14]);
  and and_19 (and_32_out[13], in_2, A[13]);
  and and_20 (and_32_out[11], in_2, A[11]);
  and and_21 (and_32_out[12], in_2, A[12]);
  Adder #(.width(32)) adder_1 (.a(and_32_out), .b(Prev), .out({Output[30:0], Last}));  // open: cin, cout
  and and_22 (and_32_out[10], in_2, A[10]);
  and and_23 (and_32_out[9], in_2, A[9]);
  and and_24 (and_32_out[7], in_2, A[7]);
  and and_25 (and_32_out[6], in_2, A[6]);
  and and_26 (and_32_out[8], in_2, A[8]);
  and and_27 (and_32_out[5], in_2, A[5]);
  and and_28 (and_32_out[4], in_2, A[4]);
  and and_29 (and_32_out[3], in_2, A[3]);
  and and_30 (and_32_out[2], in_2, A[2]);
  and and_31 (and_32_out[1], in_2, A[1]);
  and and_32 (and_32_out[0], in_2, A[0]);

  assign Output[31] = 1'b0;
endmodule

module SignDivider (
  input  [31:0] A,
  input  [31:0] B,
  output [31:0] Lo,
  output [31:0] Hi
);

  wire dif_sign;
  wire [31:0] divider_1_out, multiplexer_1_out, multiplexer_2_out, multiplier_1_out, multiplier_2_out,
       multiplier_3_out;

  // Probe on A
  // Probe on B
  Multiplier #(.width(32)) multiplier_1 (.a(A), .b({32{1'b1}}), .out(multiplier_1_out));  // open: cin, cout
  Multiplier #(.width(32)) multiplier_2 (.a({32{1'b1}}), .b(B), .out(multiplier_2_out));  // open: cin, cout
  Multiplexer #(.width(32), .enable("false")) multiplexer_1 (
    .in0(A), .in1(multiplier_1_out), .out(multiplexer_1_out), .sel(A[31]));
  xor xor_1 (dif_sign, A[31], B[31]);
  Multiplexer #(.width(32), .enable("false")) multiplexer_2 (
    .in0(B), .in1(multiplier_2_out), .out(multiplexer_2_out), .sel(B[31]));
  // Probe on multiplexer_1_out
  // Probe on multiplexer_2_out
  // Probe on divider_1_out
  Divider #(.width(32)) divider_1 (
    .a(multiplexer_1_out), .b(multiplexer_2_out), .out(divider_1_out), .rem(Hi));  // open: upper
  Multiplier #(.width(32)) multiplier_3 (.a(divider_1_out), .b({32{1'b1}}), .out(multiplier_3_out));  // open: cin, cout
  Multiplexer #(.width(32), .enable("false")) multiplexer_3 (
    .in0(divider_1_out), .in1(multiplier_3_out), .out(Lo), .sel(dif_sign));
  // Probe on Lo
  // Probe on Hi
endmodule
